# Fritzing sketch Reloj_OLED (saved by Fritzing 0.9.3b)

parts:
  Part1 = Arduino Pro Mini v13
  OLED1 = OLED 128x64 I2C Monochrome Display

nets:
  N1: Part1.A4, OLED1.SDA
  N2: Part1.A5, OLED1.SCK
  GND: Part1.GND, OLED1.GND
  VCC: Part1.VCC, OLED1.VDD
